# Fritzing sketch LCD1602_direct (saved by Fritzing 0.9.3b)

parts:
  R1 = Resistor [tolerance=±5% resistance=1k package=THT]
  LCD1 = LCD screen
  R2 = Resistor [tolerance=±5% resistance=10k package=THT]
  R3 = Resistor [tolerance=±5% resistance=330 package=THT]  # not connected
  M1 = BluePill

nets:
  N1: R1.Pin_0, LCD1.V0, R2.Pin_0
  VSS: LCD1.VSS, M1.GND
  VDD: LCD1.VDD, M1.5V
  N2: LCD1.RS, M1.A2
  N3: LCD1.R/W, M1.A1
  N4: LCD1.E, M1.A3
  N5: LCD1.DB4, M1.A4
  N6: LCD1.DB5, M1.A5
  N7: LCD1.DB6, M1.A6
  N8: LCD1.DB7, M1.A7
  N9: LCD1.LED-, M1.A0

notes:
  5V
  GND

custom parts:
  BluePill: Generic ebay blue pill STM32F103C8 "Blue pill" CPU module. Arm Cortex M3 128KB flash (usually) 20kb ram, RTC on board. Supported by the Arduino IDE for programming. As cheap as an Arduino nano but with more power and memory.
