# Fritzing sketch LCD1602_i2c (saved by Fritzing 0.9.3b)

parts:
  M1 = BluePill
  Bauteil1 = LCD1602-I2C

nets:
  N1: M1.B6, Bauteil1.SCL
  N2: M1.B7, Bauteil1.SDA
  5V: M1.5V, Bauteil1.VCC
  GND: M1.GND, Bauteil1.GND

notes:
  5V

custom parts:
  BluePill: Generic ebay blue pill STM32F103C8 "Blue pill" CPU module. Arm Cortex M3 128KB flash (usually) 20kb ram, RTC on board. Supported by the Arduino IDE for programming. As cheap as an Arduino nano but with more power and memory.
  LCD1602-I2C: A standard character display, usually with 2x16 characters. Comes in many colors with LCM1602 IIC attached.
